// Logisim project schematic.circ as structural Verilog: 2 circuits, main circuit main
module main (
  output [15:0] out_1,
  output [15:0] out_2,
  output [15:0] out_3
);

  wire clock_1_out;
  wire [1:0] counter_1_q;
  wire [9:2] rom_2_data;
  wire [15:0] alu_1_o, counter_2_q, register_1_q, register_2_q, register_3_q, rom_2_data_2;

  Clock clock_1 (.out(clock_1_out));
  Counter #(.max('h3), .width(2)) counter_1 (
    .Q(counter_1_q), .clk(clock_1_out));  // open: load, D, count, carry, up, clr
  RAM #(.addrWidth(16), .dataWidth(16), .readbehav("war"), .\type ("nonvolatile")) ram_1 (
    .addr(register_1_q), .we(out_3[9]), .oe(clock_1_out), .clk(clock_1_out), .din(out_1), .dout(out_2));
  ROM #(.addrWidth(10), .dataWidth(16)) rom_1 (.addr({rom_2_data, counter_1_q}), .data(out_3));
  Register #(.width(16)) register_1 (.D(out_1), .en(out_3[8]), .clk(clock_1_out), .Q(register_1_q));  // open: clr
  assign out_1 = out_3[10] ? out_2 : 16'bz;  // Controlled_Buffer controlled_buffer_1
  assign out_1 = out_3[2] ? register_2_q : 16'bz;  // Controlled_Buffer controlled_buffer_2
  assign out_1 = out_3[4] ? register_3_q : 16'bz;  // Controlled_Buffer controlled_buffer_3
  assign out_1 = out_3[5] ? rom_2_data_2 : 16'bz;  // Controlled_Buffer controlled_buffer_4
  assign out_1 = out_3[0] ? alu_1_o : 16'bz;  // Controlled_Buffer controlled_buffer_5
  Register #(.width(16)) register_2 (.D(out_1), .en(out_3[1]), .clk(clock_1_out), .Q(register_2_q));  // open: clr
  Register #(.width(16)) register_3 (.D(out_1), .en(out_3[3]), .clk(clock_1_out), .Q(register_3_q));  // open: clr
  ALU alu_1 (.INPUT1(register_2_q), .INPUT2(register_3_q), .OPERATOR(out_3[7]), .O(alu_1_o));
  ROM #(.addrWidth(16), .dataWidth(24)) rom_2 (.addr(counter_2_q), .data({rom_2_data, rom_2_data_2}));
  Counter #(.max('hffff), .width(16)) counter_2 (
    .load(out_3[11]), .D(rom_2_data_2), .count(out_3[6]), .Q(counter_2_q), .clk(clock_1_out));  // open: carry, up, clr

  // Notes on the sheet:
  //   contents of rom_1 (hex, n*v repeats v):
  //   4*0 22 0 0 40 28 0 0 40 3 0 0 40 83 0 0 40 120 204 0 40 120 402 0 40 800 0 0 40
  //   11  10  9  8  7  6  5  4  3  2  1
  //   11: RAM OUT 10: RAM IN 9: MAR IN 8: ALU OP 7:COUNTER INC 6: OPP OUT 5: R2 OUT 4: R2 IN 3: R1 OUT 2: R1 IN 1: ALU OUT
  //   opcode
  //   operand 1
  //   contents of rom_2 (hex, n*v repeats v):
  //   10000 20001 30000 70000
endmodule

module ALU (
  input  [15:0] INPUT1,
  input  [15:0] INPUT2,
  input  OPERATOR,
  output [15:0] O
);

  wire [1:1] not_1_out;
  wire [15:0] adder_1_out, demultiplexer_1_out0, demultiplexer_1_out1, demultiplexer_1_out2,
       demultiplexer_1_out3, divider_1_out, multiplier_1_out, subtractor_1_out;

  Demultiplexer #(.select(2), .width(16)) demultiplexer_1 (
    .out0(demultiplexer_1_out0), .out1(demultiplexer_1_out1), .out2(demultiplexer_1_out2),
    .out3(demultiplexer_1_out3), .in(INPUT1), .sel({not_1_out[1], OPERATOR}));
  Adder #(.width(16)) adder_1 (.a(demultiplexer_1_out0), .b(INPUT2), .out(adder_1_out));  // open: cin, cout
  Subtractor #(.width(16)) subtractor_1 (
    .a(demultiplexer_1_out1), .b(INPUT2), .out(subtractor_1_out));  // open: bin, bout
  Multiplier #(.width(16)) multiplier_1 (
    .a(demultiplexer_1_out2), .b(INPUT2), .out(multiplier_1_out));  // open: cin, cout
  Divider #(.width(16)) divider_1 (.a(demultiplexer_1_out3), .b(INPUT2), .out(divider_1_out));  // open: upper, rem
  Multiplexer #(.select(2), .width(16)) multiplexer_1 (
    .in0(adder_1_out), .in1(subtractor_1_out), .in2(multiplier_1_out), .in3(divider_1_out), .out(O),
    .sel({not_1_out[1], OPERATOR}));
  not not_1 (not_1_out[1], 1'b1);
endmodule
