// Logisim project schematic.circ as structural Verilog: 7 circuits, main circuit main
module main (
  input  in_1,
  input  in_2,
  output [23:0] out_3,
  output [15:0] out_4,
  output [15:0] out_5
);

  wire clock_1_out, cmp_1_out_2, controlled_buffer_5_out, controlled_buffer_8_out, gpu_1_clk, gpu_1_write,
       jnz_1_out_9, multiplexer_1_out, not_1_out, not_2_out;
  wire [4:0] gpu_1_x, gpu_1_y;
  wire [7:0] not_3_out;
  wire [9:0] register_3_q_2;
  wire [10:0] counter_1_q;
  wire [13:0] rom_1_data;
  wire [15:0] alu_1_out_5, controlled_buffer_1_out, controlled_buffer_2_out, controlled_buffer_3_out,
       controlled_buffer_4_out, controlled_buffer_10_out, gpu_1_color, ram_1_dout, register_1_q;
  wire [15:10] register_3_q;
  wire [23:0] counter_2_q, rom_2_data;

  and and_1 (counter_1_q[10], jnz_1_out_9, cmp_1_out_2);
  JNZ jnz_1 (
    .in_1(rom_2_data[23]), .in_2(rom_2_data[22]), .in_3(rom_2_data[21]), .in_4(rom_2_data[20]),
    .in_5(rom_2_data[19]), .in_6(rom_2_data[18]), .in_7(rom_2_data[17]), .in_8(rom_2_data[16]),
    .out_9(jnz_1_out_9));
  Clock clock_1 (.out(clock_1_out));
  not not_1 (not_1_out, clock_1_out);
  Counter #(.max('h4), .trigger("falling"), .width(2)) counter_1 (
    .Q(counter_1_q[1:0]), .clk(not_1_out));  // open: load, D, count, carry, up, clr
  ROM #(.addrWidth(11), .dataWidth(14)) rom_1 (
    .addr({counter_1_q[10], rom_2_data[23:16], counter_1_q[1:0]}), .data(rom_1_data));
  Multiplexer multiplexer_1 (.in0(clock_1_out), .in1(in_1), .out(multiplexer_1_out), .sel(in_2));
  GPU gpu_1 (
    .CLOCK(clock_1_out), .ADDRESS(register_3_q_2), .ALLOW_WRITE(rom_1_data[13]), .GPU_WRITE(rom_1_data[13]),
    .DATA(out_4), .X(gpu_1_x), .WRITE(gpu_1_write), .COLOR(gpu_1_color), .Y(gpu_1_y), .CLK(gpu_1_clk));
  assign controlled_buffer_1_out = rom_1_data[4] ? controlled_buffer_3_out : 16'bz;  // Controlled_Buffer controlled_buffer_1
  RAM #(.addrWidth(16), .dataWidth(16)) ram_1 (
    .addr(register_1_q), .we(rom_1_data[5]), .clk(multiplexer_1_out), .din(controlled_buffer_2_out),
    .dout(ram_1_dout));  // open: oe
  assign controlled_buffer_2_out = rom_1_data[5] ? controlled_buffer_3_out : 16'bz;  // Controlled_Buffer controlled_buffer_2
  Register #(.trigger("high"), .width(16)) register_1 (
    .D(controlled_buffer_1_out), .clk(rom_1_data[4]), .Q(register_1_q));  // open: en, clr
  assign controlled_buffer_3_out = rom_1_data[6] ? ram_1_dout : 16'bz;  // Controlled_Buffer controlled_buffer_3
  // RGB_Video #(.height(32), .scale(8), .width(32)) rgb_video_1: pin names not known; wires that end beside it: gpu_1_clk, gpu_1_write, gpu_1_x, gpu_1_y, gpu_1_color
  assign controlled_buffer_4_out = rom_1_data[2] ? controlled_buffer_3_out : 16'bz;  // Controlled_Buffer controlled_buffer_4
  assign controlled_buffer_5_out = rom_1_data[2] ? clock_1_out : 1'bz;  // Controlled_Buffer controlled_buffer_5
  assign controlled_buffer_3_out = rom_1_data[7] ? alu_1_out_5 : 16'bz;  // Controlled_Buffer controlled_buffer_6
  Register #(.width(16)) register_2 (
    .D(controlled_buffer_4_out), .clk(controlled_buffer_5_out), .Q(out_4));  // open: en, clr
  assign controlled_buffer_3_out = rom_1_data[0] ? out_4 : 16'bz;  // Controlled_Buffer controlled_buffer_7
  assign controlled_buffer_8_out = rom_1_data[3] ? clock_1_out : 1'bz;  // Controlled_Buffer controlled_buffer_8
  assign rom_1_data[9] = rom_1_data[1] ? rom_1_data[8] : 1'bz;  // Controlled_Buffer controlled_buffer_9
  assign controlled_buffer_10_out = rom_1_data[3] ? controlled_buffer_3_out : 16'bz;  // Controlled_Buffer controlled_buffer_10
  Register #(.width(16)) register_3 (
    .D(controlled_buffer_10_out), .clk(controlled_buffer_8_out), .Q({register_3_q, register_3_q_2}));  // open: en, clr
  assign controlled_buffer_3_out = rom_1_data[1] ? {register_3_q, register_3_q_2} : 16'bz;  // Controlled_Buffer controlled_buffer_11
  assign rom_1_data[9] = rom_1_data[8] ? not_2_out : 1'bz;  // Controlled_Buffer controlled_buffer_12
  not not_2 (not_2_out, rom_1_data[8]);
  CMP cmp_1 (.in_1(out_4), .out_2(cmp_1_out_2));
  assign controlled_buffer_3_out = rom_1_data[10] ? rom_2_data[15:0] : 16'bz;  // Controlled_Buffer controlled_buffer_13
  ALU alu_1 (
    .in_1(out_4), .in_2({register_3_q, register_3_q_2}), .ADDSUB(rom_1_data[9]), .CLK(clock_1_out),
    .out_5(alu_1_out_5));
  assign not_3_out = ~{8{1'b1}};  // NOT_Gate not_3, 8 bits wide
  Counter #(.max('hffffff), .trigger("falling"), .width(24)) counter_2 (
    .load(rom_1_data[12]), .clk(rom_1_data[11]), .D(out_3), .Q(counter_2_q));  // open: clr, up, count, carry
  assign out_3 = {{8{1'b0}}, rom_2_data[15:0]};  // Bit_Extender bit_extender_1
  ROM #(.addrWidth(24), .dataWidth(24)) rom_2 (.addr(counter_2_q), .data(rom_2_data));

  assign out_5 = out_4;

  // Notes on the sheet:
  //   THIS WIRE CAN NOW ONLY BE ACTIVE IF THE INS IS JNZ ->
  //   LADDR
  //   AW
  //   CE
  //   OO
  //   ALU SUB
  //   ALU ADD
  //   ALU OUT
  //   contents of rom_1 (hex, n*v repeats v):
  //   4*0 404 0 0 800 408 0 0 800 410 21 0 800 410 22 0 800 100 84 0 800 200 84 0 800 1000 0 0 800 0 0 0
  //   800 0 410 44 800 0 410 48 800 2000 0 0 800 1008*0 1000 0 0 800
  //   RAM OUT
  //   RAM IN
  //   RAM
  //   MAR IN
  //   RB IN
  //   RA IN
  //   RB OUT
  //   RA OUT
  //   RA
  //   RB
  //   TOP = Operand
  //   OPERAND LINE
  //   contents of rom_2 (hex, n*v repeats v):
  //   103e8 20002 b0000 20022 b0000 20042 b0000 20043 b0000 20044 b0000 20062 b0000 20082 b0000 20003
  //   b0000 20004 b0000 20005 b0000 20025 b0000 20045 b0000 20065 b0000 20085 b0000 20007 b0000 20027
  //   b0000 20047 b0000 20067 b0000 20087 b0000 20008 b0000 20029 b0000 20048 b0000 20069 b0000 20088
  //   b0000 2000b b0000 2000c b0000 2000d b0000 2002b b0000 2004b b0000 2006b b0000 2008b b0000 2008c
  //   b0000 2008d b0000 20010 b0000 20011 b0000 20030 b0000 20032 b0000 20050 b0000 20052 b0000 20072
  //   b0000 20070 b0000 20090 b0000 20091 b0000 20015 b0000 20016 b0000 20035 b0000 20055 b0000 20056
  //   b0000 20075 b0000 20095 b0000 20096 b0000 20097 20098 20019 b0000 2001a b0000 20039 b0000 20059
  //   b0000 2005a b0000 20079 b0000 20099 b0000 70000
endmodule

module ALU (
  input  [15:0] in_1,
  input  [15:0] in_2,
  input  ADDSUB,
  input  CLK,
  output [15:0] out_5
);

  wire register_1_q;
  wire [15:0] adder_1_out, subtractor_1_out;

  Register #(.width(1)) register_1 (.D(ADDSUB), .clk(CLK), .Q(register_1_q));  // open: en, clr
  Adder #(.width(16)) adder_1 (.a(in_1), .b(in_2), .out(adder_1_out));  // open: cin, cout
  Subtractor #(.width(16)) subtractor_1 (.a(in_1), .b(in_2), .out(subtractor_1_out));  // open: bin, bout
  Multiplexer #(.width(16)) multiplexer_1 (.in0(adder_1_out), .in1(subtractor_1_out), .out(out_5), .sel(register_1_q));

  // Notes on the sheet:
  //   0 = ADD 1 = SUB
endmodule

module CMP (
  input  [15:0] in_1,
  output out_2
);

  wire or_1_out, or_2_out, or_3_out, or_4_out, or_5_out, or_6_out, or_7_out, or_8_out, or_9_out, or_10_out,
       or_11_out, or_12_out, or_13_out, or_14_out;

  or or_1 (or_1_out, in_1[0], in_1[1]);
  or or_2 (or_2_out, in_1[2], in_1[3]);
  or or_3 (or_3_out, in_1[4], in_1[5]);
  or or_4 (or_4_out, in_1[6], in_1[7]);
  or or_5 (or_5_out, in_1[8], in_1[9]);
  or or_6 (or_6_out, in_1[10], in_1[11]);
  or or_7 (or_7_out, in_1[12], in_1[13]);
  or or_8 (or_8_out, in_1[14], in_1[15]);
  or or_9 (or_9_out, or_1_out, or_2_out);
  or or_10 (or_10_out, or_9_out, or_11_out);
  or or_11 (or_11_out, or_3_out, or_4_out);
  or or_12 (or_12_out, or_5_out, or_6_out);
  or or_13 (or_13_out, or_12_out, or_14_out);
  or or_14 (or_14_out, or_7_out, or_8_out);
  or or_15 (out_2, or_10_out, or_13_out);
endmodule

module JNZ (
  input  in_1,
  input  in_2,
  input  in_3,
  input  in_4,
  input  in_5,
  input  in_6,
  input  in_7,
  input  in_8,
  output out_9
);

  wire not_1_out, not_2_out, not_3_out, not_4_out, not_5_out, not_6_out, not_7_out;

  not not_1 (not_1_out, in_1);
  not not_2 (not_2_out, in_2);
  not not_3 (not_3_out, in_3);
  not not_4 (not_4_out, in_4);
  not not_5 (not_5_out, in_6);
  not not_6 (not_6_out, in_7);
  not not_7 (not_7_out, in_8);
  and and_1 (out_9, not_1_out, not_2_out, not_3_out, not_4_out, in_5, not_5_out, not_6_out, not_7_out);

  // Notes on the sheet:
  //   0 = !JNZ 1 = JNZ
endmodule

module GPU (
  input  CLOCK,
  input  [9:0] ADDRESS,
  input  ALLOW_WRITE,
  input  GPU_WRITE,
  input  [15:0] DATA,
  output [4:0] X,
  output WRITE,
  output [15:0] COLOR,
  output [4:0] Y,
  output CLK
);

  wire counter_1_carry, counter_2_carry;
  wire [9:0] counter_4_q, register_1_q;

  Counter #(.max('h1), .width(1)) counter_1 (.clk(CLOCK), .carry(counter_1_carry));  // open: clr, load, up, count, D, Q
  Counter #(.max('h1f), .width(5)) counter_2 (
    .clk(counter_1_carry), .carry(counter_2_carry), .Q(X));  // open: clr, load, up, count, D
  Counter #(.max('h1f), .width(5)) counter_3 (.clk(counter_2_carry), .Q(Y));  // open: clr, load, up, count, D, carry
  Counter #(.max('h3ff), .width(10)) counter_4 (
    .clk(counter_1_carry), .Q(counter_4_q));  // open: clr, load, up, count, D, carry
  Register #(.width(10)) register_1 (.D(ADDRESS), .en(ALLOW_WRITE), .clk(CLOCK), .Q(register_1_q));  // open: clr
  DUALPORTRAM dualportram_1 (
    .WR_ADDR(register_1_q), .RAMCLK(CLOCK), .WE(GPU_WRITE), .B_RD_ADDR(counter_4_q), .DIN(DATA), .BOUT(COLOR));  // open: A_RD_ADDR, RAMCLR, AOUT, out_9, WR_CYCLE

  assign CLK = CLOCK;
  assign WRITE = CLOCK;
endmodule

module DUALPORTRAM (
  input  [9:0] WR_ADDR,
  input  [9:0] A_RD_ADDR,
  input  RAMCLK,
  input  WE,
  input  [9:0] B_RD_ADDR,
  input  [15:0] DIN,
  input  RAMCLR,
  output [15:0] AOUT,
  output [9:0] out_9,
  output [15:0] BOUT,
  output WR_CYCLE
);

  wire counter_1_carry, CYCLE_1, WE_Cycle_0;
  wire [9:0] multiplexer_1_out;
  wire [15:0] ram_1_dout, ram_2_dout;

  and and_1 (WE_Cycle_0, WR_CYCLE, WE);
  Counter #(.max('h1), .width(1)) counter_1 (
    .clr(RAMCLR), .load(1'b0), .up(1'b1), .count(1'b1), .clk(RAMCLK), .carry(counter_1_carry));  // open: D, Q
  Multiplexer #(.width(10)) multiplexer_1 (.in0(WR_ADDR), .in1(A_RD_ADDR), .out(multiplexer_1_out), .sel(CYCLE_1));
  Multiplexer #(.width(10)) multiplexer_2 (.in0(WR_ADDR), .in1(B_RD_ADDR), .out(out_9), .sel(CYCLE_1));
  RAM #(.addrWidth(10), .clearpin("true"), .dataWidth(16), .enables("line")) ram_1 (
    .addr(multiplexer_1_out), .we(WE_Cycle_0), .clk(RAMCLK), .din(DIN), .dout(ram_1_dout), .clr(RAMCLR));
  RAM #(.addrWidth(10), .clearpin("true"), .dataWidth(16), .enables("line")) ram_2 (
    .addr(out_9), .we(WE_Cycle_0), .clk(RAMCLK), .din(DIN), .dout(ram_2_dout), .clr(RAMCLR));
  Comparator #(.width(1)) comparator_1 (.a(1'b0), .b(counter_1_carry), .eq(WR_CYCLE));  // open: gt, lt
  Comparator #(.width(1)) comparator_2 (.a(1'b1), .b(counter_1_carry), .eq(CYCLE_1));  // open: gt, lt
  Register #(.width(16)) register_1 (.D(ram_1_dout), .en(CYCLE_1), .clk(RAMCLK), .Q(AOUT), .clr(RAMCLR));
  Register #(.width(16)) register_2 (.D(ram_2_dout), .en(CYCLE_1), .clk(RAMCLK), .Q(BOUT), .clr(RAMCLR));

  // Other names for the same wires on the sheet: CYCLE_0 = WR_CYCLE
endmodule

module GPUTEST (
  input  [7:0] in_1,
  input  in_2,
  input  in_3,
  input  [3:0] in_4
);

  wire clock_1_out, gpu_1_p6, gpu_1_p7, gpu_1_p8, gpu_1_p9, gpu_1_p10;

  Clock clock_1 (.out(clock_1_out));
  // GPU gpu_1: pin names not known; wires that end beside it: clock_1_out, in_1, in_2, in_3, in_4, gpu_1_p6, gpu_1_p7, gpu_1_p8, gpu_1_p9, gpu_1_p10
  // RGB_Video #(.height(16), .scale(8), .width(16)) rgb_video_1: pin names not known; wires that end beside it: gpu_1_p10, gpu_1_p7, gpu_1_p6, gpu_1_p9, gpu_1_p8
endmodule
